# Fritzing sketch Current_sensor (saved by Fritzing 0.9.3b)
breadboards: 1

parts:
  Componente1 = Arduino Nano (Rev3.0)
  PSU1 = Adjustable Breadboard Power Supply
  U1 = LM358 [package=dip08]
  R1 = Resistor [tolerance=±5% resistance=1k package=THT]
  R2 = Resistor [tolerance=±1% resistance=3.8k package=THT]
  L1 = Inductor [package="0805 [SMD]"]

nets:
  N1: Componente1.GND, PSU1.Vout+, PSU1.Vin-, R1.Pin_0, L1.pin_1
  N2: Componente1.A0, U1.G$1_OUT, R2.Pin_1
  N3: PSU1.Vout-, U1.G$1_V-
  N4: PSU1.Vin+, U1.G$1_V+
  N5: U1.G$1_-IN, R1.Pin_1, R2.Pin_0
  N6: U1.G$1_+IN, L1.pin_0
